# Fritzing sketch CARARM (saved by Fritzing 0.9.3b)
breadboards: 1

parts:
  U1 = ESP8266 NodeMCU LoLin module
  J1 = Basic Servo
  J2 = Basic Servo
  J3 = Basic Servo
  C1 = Electrolytic Capacitor [capacitance=100μF package="0807 [SMD, electrolytic]"]
  J4 = Basic Servo

nets:
  N1: U1.D1, J1.pulse
  N2: U1.D2, J2.pulse
  N3: U1.D3, J3.pulse
  N4: U1.D4, J4.pulse
  GND: U1.GND, J1.gnd, J2.gnd, J3.gnd, C1.-, J4.gnd
  VCC: U1.Vin, J1.vcc, J2.vcc, J3.vcc, C1.+, J4.vcc

custom parts:
  ESP8266 NodeMCU LoLin module: ESP8266 based NodeMCU
